# Fritzing sketch Flux Fritzing (saved by Fritzing 0.9.4)

parts:
  MCU1 = Raspberry Pi Zero
  NEOPIXEL1 = Neopixel Strip -- Black (60/m) [part_number=1461]

nets:
  N1: MCU1.pin_2, MCU1.pin_4, NEOPIXEL1.+5V
  N2: MCU1.pin_6, MCU1.pin_9, NEOPIXEL1.GND
  N3: MCU1.pin_32, NEOPIXEL1.DI

custom parts:
  Neopixel Strip -- Black (60/m): Neopixel Strip, Black, 60 pixels per meter.
